// Logisim project Data Memory.circ as structural Verilog: 1 circuit, main circuit Data Memory
module Data_Memory (
  input  [3:0] Address,
  input  [3:0] Write_Data,
  input  MemoryWrite,
  input  MemoryRead,
  input  CLK,
  output [3:0] MemoryData
);

  RAM #(.addrWidth(4), .dataWidth(4), .bus("separate")) ram_1 (
    .addr(Address), .din(Write_Data), .data(MemoryData), .str(MemoryWrite), .clk(CLK), .ld(MemoryRead));  // open: sel, clr
endmodule
