// Logisim project MIPS.circ as structural Verilog: 9 circuits, main circuit Reg-file
module Reg_file (
  input  [3:0] Reg_1_Adress,
  input  [3:0] Reg_2_Adress,
  input  [3:0] Write_data,
  input  [3:0] reg_write_address,
  input  RegWrite,
  input  CLK,
  output [3:0] Read_data_1,
  output [3:0] Read_data_2,
  output [3:0] t0,
  output [3:0] t1,
  output [3:0] t2,
  output [3:0] t3,
  output [3:0] t4
);

  wire and_1_out, decoder_1_out1, decoder_1_out2, decoder_1_out3, decoder_1_out4, decoder_1_out5,
       decoder_1_out6;
  wire [2:0] multiplexer_1_out;
  wire [3:0] register_1_o_sp;

  Multiplexer #(.width(3), .enable("false")) multiplexer_1 (
    .in0(3'b000), .in1(reg_write_address[2:0]), .out(multiplexer_1_out), .sel(and_1_out));
  and and_1 (and_1_out, RegWrite, CLK);
  Decoder #(.select(3), .enable("false")) decoder_1 (
    .out1(decoder_1_out1), .out2(decoder_1_out2), .out3(decoder_1_out3), .out4(decoder_1_out4),
    .out5(decoder_1_out5), .out6(decoder_1_out6), .sel(multiplexer_1_out));  // open: out0, out7
  register register_1 (
    .t0(Write_data), .CLK0(decoder_1_out1), .t1(Write_data), .CLK1(decoder_1_out2), .t2(Write_data),
    .CLK2(decoder_1_out3), .t3(Write_data), .CLK3(decoder_1_out4), .t4(Write_data), .CLK4(decoder_1_out5),
    .sp(Write_data), .CLKSP(decoder_1_out6), .O_t0(t0), .O_t1(t1), .O_t2(t2), .O_t3(t3), .O_t4(t4),
    .O_sp(register_1_o_sp));
  Multiplexer #(.select(3), .width(4), .enable("false")) multiplexer_2 (
    .in0(4'b0000), .in1(t0), .in2(t1), .in3(t2), .in4(t3), .in5(t4), .in6(register_1_o_sp),
    .out(Read_data_1), .sel(Reg_1_Adress[2:0]));  // open: in7
  Multiplexer #(.select(3), .width(4), .enable("false")) multiplexer_3 (
    .in0(4'b0000), .in1(t0), .in2(t1), .in3(t2), .in4(t3), .in5(t4), .in6(register_1_o_sp),
    .out(Read_data_2), .sel(Reg_2_Adress[2:0]));  // open: in7
endmodule

module register (
  input  [3:0] t0,
  input  CLK0,
  input  [3:0] t1,
  input  CLK1,
  input  [3:0] t2,
  input  CLK2,
  input  [3:0] t3,
  input  CLK3,
  input  [3:0] t4,
  input  CLK4,
  input  [3:0] sp,
  input  CLKSP,
  output [3:0] O_t0,
  output [3:0] O_t1,
  output [3:0] O_t2,
  output [3:0] O_t3,
  output [3:0] O_t4,
  output [3:0] O_sp
);

  wire n7474_13_p3;
  wire [3:0] n7474_11_p3;

  // _7474 7474_1: pin names not known; wires that end beside it: t0[0], CLK0, O_t0[0], t0[1], CLK0, O_t0[1]
  // _7474 7474_2: pin names not known; wires that end beside it: t0[2], CLK0, O_t0[2], t0[3], CLK0, O_t0[3]
  // _7474 7474_3: pin names not known; wires that end beside it: t1[0], CLK1, O_t1[0], t1[1], CLK1, O_t1[1]
  // _7474 7474_4: pin names not known; wires that end beside it: t1[2], CLK1, O_t1[2], t1[3], CLK1
  // _7474 7474_5: pin names not known; wires that end beside it: t2[0], CLK2, O_t2[0], O_t1[3], t2[1], CLK2, O_t2[1]
  // _7474 7474_6: pin names not known; wires that end beside it: t2[2], CLK2, O_t2[2], t2[3], CLK2, O_t2[3]
  // _7474 7474_7: pin names not known; wires that end beside it: t3[0], CLK3, O_t3[0], t3[1], CLK3, O_t3[1]
  // _7474 7474_8: pin names not known; wires that end beside it: t3[2], CLK3, O_t3[2], t3[3], CLK3, O_t3[3]
  // _7474 7474_9: pin names not known; wires that end beside it: t4[0], CLK4, O_t4[0], t4[1], CLK4, O_t4[1]
  // _7474 7474_10: pin names not known; wires that end beside it: t4[2], CLK4, O_t4[2], t4[3], CLK4, O_t4[3]
  // _7474 7474_11: pin names not known; wires that end beside it: sp[0], CLKSP, n7474_11_p3[0], sp[1], CLKSP, n7474_11_p3[1]
  // _7474 7474_12: pin names not known; wires that end beside it: sp[2], CLKSP, n7474_11_p3[2], sp[3], CLKSP, n7474_11_p3[3]
  Multiplexer #(.width(4), .enable("false")) multiplexer_1 (
    .in0(4'b1111), .in1(n7474_11_p3), .out(O_sp), .sel(n7474_13_p3));
  // _7474 7474_13: pin names not known; wires that end beside it: 1'b1, CLKSP, n7474_13_p3, 1'b0, 1'b1
endmodule

module ControlUnit (
  input  [3:0] Opcode,
  output [11:0] out_2,
  output jump,
  output RegDst,
  output RegWrite,
  output MemRead,
  output MemWrite,
  output MemtoReg,
  output beq,
  output bneq,
  output ALUsrc,
  output [2:0] ALUop
);

  ROM #(.addrWidth(4), .dataWidth(12)) rom_1 (
    .addr(Opcode), .data({ALUop, ALUsrc, bneq, beq, MemtoReg, MemWrite, MemRead, out_2[2:1], jump}));  // open: sel

  assign {out_2[11:3], out_2[0]} = {ALUop, ALUsrc, bneq, beq, MemtoReg, MemWrite, MemRead, jump};
  assign RegDst = out_2[1];
  assign RegWrite = out_2[2];

  // Notes on the sheet:
  //   contents of rom_1 (hex, n*v repeats v):
  //   b04 280 240 504 6 806 606 104 304 110 12c 704 1 206 d04 406
endmodule

module Instr_Memory (
  input  [7:0] PC,
  output [3:0] Dest_shamt_addrs_imd_0_3,
  output [3:0] srcreg2_4_7,
  output [3:0] srcreg1_8_11,
  output [3:0] Opcode_12_15,
  output [7:0] Target_Address_0_7
);

  ROM #(.dataWidth(16)) rom_1 (
    .addr(PC), .data({Opcode_12_15, srcreg1_8_11, srcreg2_4_7, Dest_shamt_addrs_imd_0_3}));  // open: sel

  assign Target_Address_0_7 = {srcreg1_8_11, srcreg2_4_7};

  // Notes on the sheet:
  //   contents of rom_1 (hex, n*v repeats v):
  //   7023 7035 4231 4134 7452 9323 222 8441 2421 c250 e441 a422 6241 f153 c220 9610 8661 9630 8661 3115
  //   7661 a610 b336 964f a342 9640 8661 a640 7661 a630 5333 7661 a630 c250 1311 8113 c0f0
endmodule

module main (
  input  [7:0] in_1,
  input  in_2,
  output [3:0] t0,
  output [3:0] t1,
  output [3:0] t2,
  output [3:0] t3,
  output [3:0] t4
);

  wire Control_Unit_alusrc, Control_Unit_beq, Control_Unit_bneq, Control_Unit_jump, Control_Unit_memread,
       Control_Unit_memtoreg, Control_Unit_memwrite, Control_Unit_regdst, Control_Unit_regwrite, n7408_1_p2,
       n7408_1_p3, n7408_1_p5, n7408_1_p6, n7474_1_p3, not_1_out, or_1_out;
  wire [2:0] Control_Unit_aluop;
  wire [3:0] ALU_output, Data_Memory_memorydata, Inst__Memory_dest_shamt_addrs_imd_0_3,
       Inst__Memory_opcode_12_15, Inst__Memory_srcreg1_8_11, Inst__Memory_srcreg2_4_7, multiplexer_2_out,
       multiplexer_4_out, multiplexer_6_out, Reg_File_read_data_1, Reg_File_read_data_2;
  wire [7:0] _8_bit_adder_out_3, _8_bit_flipflop_q, adder_1_out, Inst__Memory_target_address_0_7,
       multiplexer_1_out, multiplexer_3_out, multiplexer_5_out;

  D_Flip_Flop_8bit _8_bit_flipflop (.D(multiplexer_5_out), .CLK(not_1_out), .Q(_8_bit_flipflop_q));
  not not_1 (not_1_out, in_2);
  Multiplexer #(.width(8), .enable("false")) multiplexer_1 (
    .in0(in_1), .in1(_8_bit_flipflop_q), .out(multiplexer_1_out), .sel(n7474_1_p3));
  // _7474 7474_1: pin names not known; wires that end beside it: 1'b1, in_2, n7474_1_p3, 1'b0, 1'b1, {8{1'b0}}
  Adder adder_1 (.a(multiplexer_1_out), .b({8{1'b0}}), .out(adder_1_out), .cin(1'b1));  // open: cout
  Instr_Memory Inst__Memory (
    .PC(multiplexer_1_out), .Dest_shamt_addrs_imd_0_3(Inst__Memory_dest_shamt_addrs_imd_0_3),
    .srcreg2_4_7(Inst__Memory_srcreg2_4_7), .srcreg1_8_11(Inst__Memory_srcreg1_8_11),
    .Opcode_12_15(Inst__Memory_opcode_12_15), .Target_Address_0_7(Inst__Memory_target_address_0_7));
  ControlUnit Control_Unit (
    .Opcode(Inst__Memory_opcode_12_15), .jump(Control_Unit_jump), .RegDst(Control_Unit_regdst),
    .RegWrite(Control_Unit_regwrite), .MemRead(Control_Unit_memread), .MemWrite(Control_Unit_memwrite),
    .MemtoReg(Control_Unit_memtoreg), .beq(Control_Unit_beq), .bneq(Control_Unit_bneq),
    .ALUsrc(Control_Unit_alusrc), .ALUop(Control_Unit_aluop));  // open: out_2
  Multiplexer #(.width(4), .enable("false")) multiplexer_2 (
    .in0(Inst__Memory_srcreg2_4_7), .in1(Inst__Memory_dest_shamt_addrs_imd_0_3), .out(multiplexer_2_out),
    .sel(Control_Unit_regdst));
  Reg_file Reg_File (
    .Reg_1_Adress(Inst__Memory_srcreg1_8_11), .Reg_2_Adress(Inst__Memory_srcreg2_4_7),
    .Write_data(multiplexer_6_out), .reg_write_address(multiplexer_2_out), .RegWrite(Control_Unit_regwrite),
    .CLK(in_2), .Read_data_1(Reg_File_read_data_1), .Read_data_2(Reg_File_read_data_2), .t0(t0), .t1(t1),
    .t2(t2), .t3(t3), .t4(t4));
  ADD_SUB_8bit _8_bit_adder (
    .in_1(adder_1_out), .in_2(Inst__Memory_dest_shamt_addrs_imd_0_3), .out_3(_8_bit_adder_out_3));
  Multiplexer #(.width(8), .enable("false")) multiplexer_3 (
    .in0(adder_1_out), .in1(_8_bit_adder_out_3), .out(multiplexer_3_out), .sel(or_1_out));
  or or_1 (or_1_out, n7408_1_p6, n7408_1_p3);
  Multiplexer #(.width(4), .enable("false")) multiplexer_4 (
    .in0(Reg_File_read_data_2), .in1(Inst__Memory_dest_shamt_addrs_imd_0_3), .out(multiplexer_4_out),
    .sel(Control_Unit_alusrc));
  // _7408 7408_1: pin names not known; wires that end beside it: Control_Unit_beq, n7408_1_p2, n7408_1_p3, Control_Unit_bneq, n7408_1_p5, n7408_1_p6
  Multiplexer #(.width(8), .enable("false")) multiplexer_5 (
    .in0(multiplexer_3_out), .in1(Inst__Memory_target_address_0_7), .out(multiplexer_5_out),
    .sel(Control_Unit_jump));
  ALU_4bit ALU (
    .A(Reg_File_read_data_1), .B(multiplexer_4_out), .ALUOp(Control_Unit_aluop), .Output(ALU_output),
    .Zero_Flag(n7408_1_p2));
  not not_2 (n7408_1_p5, n7408_1_p2);
  Data_Memory Data_Memory (
    .Address(ALU_output), .Write_Data(Reg_File_read_data_2), .MemoryWrite(Control_Unit_memwrite),
    .MemoryRead(Control_Unit_memread), .CLK(in_2), .MemoryData(Data_Memory_memorydata));
  Multiplexer #(.width(4), .enable("false")) multiplexer_6 (
    .in0(ALU_output), .in1(Data_Memory_memorydata), .out(multiplexer_6_out), .sel(Control_Unit_memtoreg));
endmodule

module ADD_SUB_8bit (
  input  [7:0] in_1,
  input  [3:0] in_2,
  output [7:0] out_3
);

  wire [7:0] adder_1_out, negator_1_out, subtractor_1_out;

  Negator negator_1 (.in({{5{in_2[3]}}, in_2[2:0]}), .out(negator_1_out));
  Adder adder_1 (.a(in_1), .b({{5{in_2[3]}}, in_2[2:0]}), .out(adder_1_out));  // open: cin, cout
  Subtractor subtractor_1 (.a(in_1), .b(negator_1_out), .out(subtractor_1_out));  // open: bin, bout
  Multiplexer #(.width(8), .enable("false")) multiplexer_1 (
    .in0(adder_1_out), .in1(subtractor_1_out), .out(out_3), .sel(in_2[3]));
endmodule

module D_Flip_Flop_8bit (
  input  [7:0] D,
  input  CLK,
  output [7:0] Q
);

  // _7474 7474_1: pin names not known; wires that end beside it: D[0], CLK, Q[0], D[1], CLK, Q[1]
  // _7474 7474_2: pin names not known; wires that end beside it: D[2], CLK, Q[2], D[3], CLK
  // _7474 7474_3: pin names not known; wires that end beside it: D[4], CLK, Q[4], Q[3], D[5], CLK, Q[5]
  // _7474 7474_4: pin names not known; wires that end beside it: D[6], CLK, Q[6], D[7], CLK, Q[7]
endmodule

module ALU_4bit (
  input  [3:0] A,
  input  [2:0] ALUOp,
  input  [3:0] B,
  output [3:0] Output,
  output Zero_Flag
);

  wire [3:0] adder_1_out, and_1_out, nor_1_out, or_1_out, shifter_1_out, shifter_2_out, subtractor_1_out;

  Adder #(.width(4)) adder_1 (.a(A), .b(B), .out(adder_1_out), .cin(1'b0));  // open: cout
  Subtractor #(.width(4)) subtractor_1 (.a(A), .b(B), .out(subtractor_1_out), .bin(1'b0));  // open: bout
  assign or_1_out = A | B;  // OR_Gate or_1, 4 bits wide
  assign and_1_out = A & B;  // AND_Gate and_1, 4 bits wide
  assign nor_1_out = ~(A | B);  // NOR_Gate nor_1, 4 bits wide
  Shifter #(.width(4)) shifter_1 (.in(A), .\dist (B[1:0]), .out(shifter_1_out));
  Shifter #(.width(4), .shift("lr")) shifter_2 (.in(A), .\dist (B[1:0]), .out(shifter_2_out));
  Multiplexer #(.select(3), .width(4), .enable("false")) multiplexer_1 (
    .in0(adder_1_out), .in1(subtractor_1_out), .in2(or_1_out), .in3(and_1_out), .in4(nor_1_out),
    .in5(shifter_1_out), .in6(shifter_2_out), .in7(4'b0000), .out(Output), .sel(ALUOp));
  nor nor_2 (Zero_Flag, Output[0], Output[1], Output[2], Output[3]);
endmodule

module Data_Memory (
  input  [3:0] Address,
  input  [3:0] Write_Data,
  input  MemoryWrite,
  input  MemoryRead,
  input  CLK,
  output [3:0] MemoryData
);

  RAM #(.addrWidth(4), .dataWidth(4), .bus("separate")) ram_1 (
    .addr(Address), .din(Write_Data), .data(MemoryData), .str(MemoryWrite), .clk(CLK), .ld(MemoryRead));  // open: sel, clr
endmodule
